// Logisim project Sumador-4-bits.circ as structural Verilog: 2 circuits, main circuit main
module main (
  input  A,
  input  in_2,
  input  in_3,
  input  in_4,
  input  in_5,
  input  B,
  input  in_7,
  input  in_8,
  input  in_9,
  output out_10,
  output out_11,
  output out_12,
  output out_13,
  output out_14
);

  wire sumadorcompleto_1_cout, sumadorcompleto_2_cout, sumadorcompleto_3_cout;

  SumadorCompleto sumadorcompleto_1 (.A(in_4), .B(in_8), .Cin(in_9), .SUMA(out_14), .Cout(sumadorcompleto_1_cout));
  SumadorCompleto sumadorcompleto_2 (
    .A(in_3), .B(in_7), .Cin(sumadorcompleto_1_cout), .SUMA(out_13), .Cout(sumadorcompleto_2_cout));
  SumadorCompleto sumadorcompleto_3 (
    .A(in_2), .B(B), .Cin(sumadorcompleto_2_cout), .SUMA(out_12), .Cout(sumadorcompleto_3_cout));
  SumadorCompleto sumadorcompleto_4 (.A(A), .B(in_5), .Cin(sumadorcompleto_3_cout), .SUMA(out_11), .Cout(out_10));
endmodule

module SumadorCompleto (
  input  A,
  input  B,
  input  Cin,
  output SUMA,
  output Cout
);

  wire and_1_out, and_2_out, xor_1_out;

  xor xor_1 (xor_1_out, A, B);
  xor xor_2 (SUMA, xor_1_out, Cin);
  and and_1 (and_1_out, A, B);
  and and_2 (and_2_out, xor_1_out, Cin);
  or or_1 (Cout, and_1_out, and_2_out);
endmodule
