// Logisim project Sumador.circ as structural Verilog: 1 circuit, main circuit Sumador
module Sumador (
  input  A,
  input  B,
  input  Cin,
  output SUMA,
  output Cout
);

  wire and_1_out, and_2_out, xor_1_out;

  xor xor_1 (xor_1_out, A, B);
  xor xor_2 (SUMA, xor_1_out, Cin);
  and and_1 (and_1_out, A, B);
  and and_2 (and_2_out, Cin, xor_1_out);
  or or_1 (Cout, and_1_out, and_2_out);
endmodule
